# Fritzing sketch control board (saved by Fritzing 0.9.2b)

parts:
  JP1 = Header 4 [package=molex-1x4_lock]
  JP2 = Header 4 [package=molex-1x4_lock]
  JP3 = Header 4 [package=molex-1x4_lock]
  JP4 = Header 4 [package=molex-1x4_lock]
  JP5 = Header 4 [package=molex-1x4_lock]
  JP6 = Header 4 [package=molex-1x4_lock]
  JP7 = Header 4 [package=molex-1x4_lock]
  JP8 = Header 4 [package=molex-1x4_lock]
  JP9 = Header 4 [package=molex-1x4_lock]
  Part1 = Arduino Mega Proto Shield (v6)

nets:
  N1: JP1.1, Part1.D52, Part1.N$467
  N2: JP1.2, Part1.D53, Part1.N$459
  N3: JP1.3, Part1.N$448
  N4: JP1.4, Part1.N$387
  N5: JP2.1, Part1.D50, Part1.N$464
  N6: JP2.2, Part1.D51, Part1.N$456
  N7: JP2.3, Part1.N$445
  N8: JP2.4, Part1.N$264
  N9: JP3.1, Part1.RX3, Part1.N$461
  N10: JP3.2, Part1.TX3, Part1.N$450
  N11: JP3.3, Part1.N$442
  N12: JP3.4, Part1.N$4
  N13: JP4.1, Part1.N$288
  N14: JP4.2, Part1.N$287
  N15: JP4.3, Part1.N$270
  N16: JP4.4, JP5.2, Part1.N$266, Part1.N$391
  N17: JP5.1, Part1.N$392
  N18: JP5.3, Part1.N$390
  N19: JP5.4, JP8.4, Part1.N$389, Part1.N$437
  N20: JP6.1, Part1.N$204
  N21: JP6.2, Part1.N$202
  N22: JP6.3, Part1.N$200
  N23: JP6.4, Part1.N$199
  N24: JP7.1, Part1.TX2, Part1.N$306
  N25: JP7.2, Part1.RX2, Part1.N$303
  N26: JP7.3, Part1.+5V, Part1.N$302
  N27: JP7.4, Part1.GND, Part1.N$301
  N28: JP8.1, JP8.3, Part1.N$438, Part1.N$440
  N29: JP8.2, Part1.N$439
  N30: JP9.1, Part1.D11, Part1.N$209
  N31: JP9.2, Part1.D12, Part1.N$208
  N32: JP9.3, Part1.N$207
  N33: JP9.4, Part1.N$206
